// Logisim project Processor.circ as structural Verilog: 15 circuits, main circuit Processor
module Processor (
  input  [3:0] Display_Address,
  input  Reset
);

  wire alu_1_is, alu_1_is_2, Call, Clock, control_unit_1_isbeq, control_unit_1_isbgt, control_unit_1_iscall,
       control_unit_1_isld, control_unit_1_isubranch, control_unit_1_iswb, control_zero_1_iscall_2,
       control_zero_1_isret_2, control_zero_1_iswb_2, flags_1_flags_e, flags_1_flags_gt,
       forwarding_unit_1_rw__ma, forwarding_unit_1_rw__of_1, forwarding_unit_1_rw__of_2, Imme, IsBT, IsStall,
       not_1_out, not_2_out, not_3_out, not_4_out, not_5_out, or_1_out, register_2_q, register_3_q,
       register_4_q, register_5_q, register_6_q, register_7_q, RETURN, St, STORE;
  wire [0:0] register_1_q, register_8_q;
  wire [1:0] control_zero_1_isload_2, forwarding_unit_1_rw__ex_1, M4, M4St, register_10_q;
  wire [1:1] not_6_out;
  wire [2:0] control_zero_1_isbeq_2, OF_EX_7_q;
  wire [3:0] IF_OF_2_q_2, multiplexer_9_out, multiplexer_10_out, multiplexer_13_out,
       register_file_1_displayd_2;
  wire [4:0] IF_OF_2_q_3;
  wire [12:0] control_unit_1_alusignals, control_zero_1_alusignal_2, OF_EX_6_q;
  wire [26:0] IF_OF_2_q;
  wire [31:0] adder_1_out, adder_2_out, adder_3_out, alu_1_aluresult, bit_extender_1_out,
       calculate_immediate_1_immx, EX_MA_2_q, EX_MA_3_q, EX_MA_4_q, EX_MA_q, IF_OF_PC_q, IF_OF_q,
       Instruction, Instruction_BL, Instruction_Post_EX, IST, MA_RW_2_q, MA_RW_3_q, MA_RW_4_q, MA_RW_q,
       memory_unit_1_ldresult, multiplexer_1_out, multiplexer_2_out, multiplexer_3_out, multiplexer_4_out,
       multiplexer_5_out, multiplexer_6_out, multiplexer_7_out, multiplexer_8_out, multiplexer_11_out,
       multiplexer_12_out, OF_EX_3_q, OF_EX_4_q, OF_EX_5_q, OF_EX_q, OP2, PC_q, register_file_1_displayd,
       register_file_1_readd1, register_file_1_readd2, shifter_1_out;

  // Probe on IF_OF_q
  // Probe on Instruction_Post_EX
  Load_Use Data_Lock (.A(IF_OF_q), .B(Instruction_Post_EX), .is_Stall(IsStall));
  Register #(.width(32)) OF_EX (.D(IF_OF_PC_q), .Q(OF_EX_q), .clk(Clock));  // open: en, clr
  // Probe on alu_1_aluresult
  not not_1 (not_1_out, IsStall);
  Register #(.width(32)) EX_MA (.D(OF_EX_q), .Q(EX_MA_q), .clk(Clock));  // open: en, clr
  // Probe on IST
  // Probe on PC_q
  Register #(.width(32), .trigger("falling")) PC (
    .D(multiplexer_1_out), .en(not_1_out), .Q(PC_q), .clk(Clock), .clr(Reset));
  Register #(.width(32)) MA_RW (.D(EX_MA_q), .Q(MA_RW_q), .clk(Clock));  // open: en, clr
  // Probe on multiplexer_8_out
  Multiplexer #(.width(32), .enable("false")) multiplexer_1 (
    .in0(adder_1_out), .in1(multiplexer_3_out), .out(multiplexer_1_out), .sel(IsBT));
  Adder #(.width(32)) adder_1 (.a(32'h4), .b(PC_q), .out(adder_1_out));  // open: cin, cout
  assign bit_extender_1_out = {{5{IF_OF_q[26]}}, IF_OF_q[26:0]};  // Bit_Extender bit_extender_1
  Register #(.width(32)) IF_OF_PC (.D(PC_q), .en(not_2_out), .Q(IF_OF_PC_q), .clk(Clock));  // open: clr
  not not_2 (not_2_out, IsStall);
  // Probe on Instruction
  // Probe on EX_MA_2_q
  // Probe on memory_unit_1_ldresult
  Register #(.width(32)) MA_RW_2 (.D(EX_MA_2_q), .Q(MA_RW_2_q), .clk(Clock));  // open: en, clr
  // Probe on IST
  Shifter #(.width(32)) shifter_1 (.in(bit_extender_1_out), .\dist (5'b00010), .out(shifter_1_out));
  Register #(.width(32)) OF_EX_2 (.D(multiplexer_5_out), .Q(OP2), .clk(Clock));  // open: en, clr
  Branch_Lock branch_lock_1 (
    .Instruction(Instruction), .is_branch_taken(IsBT), .Instruction_2(Instruction_BL));  // open: Branch_Target, Immediate, Operand, Branch_Target_2, Immediate_2, Operand_2
  // Probe on multiplexer_12_out
  ALU alu_1 (
    .A(multiplexer_12_out), .B(multiplexer_8_out), .ALUsignals(OF_EX_6_q), .aluResult(alu_1_aluresult),
    .is(alu_1_is), .is_2(alu_1_is_2));
  Register #(.width(32)) EX_MA_2 (.D(alu_1_aluresult), .Q(EX_MA_2_q), .clk(Clock));  // open: en, clr
  Adder #(.width(32)) adder_2 (.a(MA_RW_q), .b(32'h4), .out(adder_2_out));  // open: cin, cout
  Multiplexer #(.select(2), .width(32), .enable("false")) multiplexer_2 (
    .in0(MA_RW_2_q), .in1(MA_RW_3_q), .in2(adder_2_out), .out(multiplexer_2_out),
    .sel({Call, register_1_q[0]}));  // open: in3
  // Probe on multiplexer_2_out
  Calculate_Immediate calculate_immediate_1 (.imm(IF_OF_q[17:0]), .immx(calculate_immediate_1_immx));
  Adder #(.width(32)) adder_3 (.a(shifter_1_out), .b(IF_OF_PC_q), .out(adder_3_out));  // open: cin, cout
  Register #(.width(32)) OF_EX_3 (.D(adder_3_out), .Q(OF_EX_3_q), .clk(Clock));  // open: en, clr
  // Probe on calculate_immediate_1_immx
  Multiplexer #(.width(32), .enable("false")) multiplexer_3 (
    .in0(OF_EX_3_q), .in1(multiplexer_12_out), .out(multiplexer_3_out), .sel(register_7_q));
  // Probe on multiplexer_7_out
  Multiplexer #(.width(32), .enable("false")) multiplexer_4 (
    .in0(EX_MA_3_q), .in1(multiplexer_2_out), .out(multiplexer_4_out), .sel(forwarding_unit_1_rw__ma));
  // Probe on multiplexer_4_out
  Memory_Unit memory_unit_1 (
    .MAR(EX_MA_2_q), .ldResult(memory_unit_1_ldresult), .MDR(multiplexer_4_out), .isSt(register_10_q[1]),
    .isLd(register_10_q[0]), .Clock(Clock), .Reset(Reset));
  Register #(.width(32)) MA_RW_3 (.D(memory_unit_1_ldresult), .Q(MA_RW_3_q), .clk(Clock));  // open: en, clr
  Clock u_Clock (.out(Clock));
  ROM #(.addrWidth(24), .dataWidth(32)) rom_1 (.addr(PC_q[25:2]), .data(IST));  // open: sel
  not not_3 (not_3_out, IsStall);
  Multiplexer #(.width(32), .enable("false")) multiplexer_5 (
    .in0(register_file_1_readd2), .in1(multiplexer_2_out), .out(multiplexer_5_out),
    .sel(forwarding_unit_1_rw__of_2));
  Multiplexer #(.width(32), .enable("false")) multiplexer_6 (
    .in0(multiplexer_5_out), .in1(calculate_immediate_1_immx), .out(multiplexer_6_out), .sel(Imme));
  Register #(.width(32)) OF_EX_4 (.D(multiplexer_6_out), .Q(OF_EX_4_q), .clk(Clock));  // open: en, clr
  Flags flags_1 (
    .isCmp(OF_EX_6_q[0]), .is(alu_1_is), .is_2(alu_1_is_2), .flags_GT(flags_1_flags_gt),
    .flags_E(flags_1_flags_e));
  Multiplexer #(.width(32), .enable("false")) multiplexer_7 (
    .in0(OP2), .in1(multiplexer_2_out), .out(multiplexer_7_out), .sel(M4[0]));
  Register #(.width(32)) EX_MA_3 (.D(multiplexer_7_out), .Q(EX_MA_3_q), .clk(Clock));  // open: en, clr
  Register #(.width(1)) register_1 (.D(register_10_q[0]), .Q(register_1_q[0]), .clk(Clock));  // open: en, clr
  Register #(.width(32)) IF_OF (.D(IST), .en(not_3_out), .Q(IF_OF_q), .clk(Clock));  // open: clr
  Multiplexer #(.select(2), .width(32), .enable("false")) multiplexer_8 (
    .in0(OF_EX_4_q), .in1(multiplexer_2_out), .in2(EX_MA_2_q), .in3(EX_MA_2_q), .out(multiplexer_8_out),
    .sel(M4St));
  Hex_Digit_Display hex_digit_display_1 (.value(register_file_1_displayd[31:28]));  // open: dp
  Register #(.width(1)) register_2 (.D(control_zero_1_iswb_2), .Q(register_2_q), .clk(Clock));  // open: en, clr
  Register #(.width(1)) register_3 (.D(register_2_q), .Q(register_3_q), .clk(Clock));  // open: en, clr
  // Probe on {IF_OF_2_q_3, IF_OF_2_q[26:18], IF_OF_2_q_2, IF_OF_2_q[13:0]}
  Register #(.width(32)) IF_OF_2 (
    .D(IST), .en(not_4_out), .Q({IF_OF_2_q_3, IF_OF_2_q[26:18], IF_OF_2_q_2, IF_OF_2_q[13:0]}), .clk(Clock));  // open: clr
  not not_4 (not_4_out, IsStall);
  Multiplexer #(.width(4), .enable("false")) multiplexer_9 (
    .in0(IF_OF_2_q_2), .in1(IF_OF_2_q[25:22]), .out(multiplexer_9_out), .sel(STORE));
  // Probe on register_file_1_readd2
  // Probe on multiplexer_11_out
  // Probe on OF_EX_5_q
  Hex_Digit_Display hex_digit_display_2 (.value(register_file_1_displayd_2));  // open: dp
  or or_1 (or_1_out, IsStall, IsBT);
  Register #(.width(1)) register_4 (.D(register_3_q), .Q(register_4_q), .clk(Clock));  // open: en, clr
  Multiplexer #(.width(4), .enable("false")) multiplexer_10 (
    .in0(IF_OF_2_q[21:18]), .in1(4'b1111), .out(multiplexer_10_out), .sel(RETURN));
  // Probe on register_file_1_readd1
  not not_5 (not_5_out, forwarding_unit_1_rw__of_1);
  Multiplexer #(.width(32), .enable("false")) multiplexer_11 (
    .in0(multiplexer_2_out), .in1(register_file_1_readd1), .out(multiplexer_11_out), .sel(not_5_out));
  Register #(.width(32)) OF_EX_5 (.D(multiplexer_11_out), .Q(OF_EX_5_q), .clk(Clock));  // open: en, clr
  Multiplexer #(.select(2), .width(32), .enable("false")) multiplexer_12 (
    .in0(OF_EX_5_q), .in1(multiplexer_2_out), .in2(EX_MA_2_q), .in3(EX_MA_2_q), .out(multiplexer_12_out),
    .sel(forwarding_unit_1_rw__ex_1));
  Hex_Digit_Display hex_digit_display_3 (.value(register_file_1_displayd[23:20]));  // open: dp
  // Probe on multiplexer_10_out
  Register_File register_file_1 (
    .ReadA1(multiplexer_10_out), .ReadA2(multiplexer_9_out), .WriteE(register_4_q),
    .WriteD(multiplexer_2_out), .ReadD1(register_file_1_readd1), .ReadD2(register_file_1_readd2),
    .Clock(Clock), .Reset(Reset),
    .DisplayD({register_file_1_displayd[31:28], register_file_1_displayd_2, register_file_1_displayd[23:0]}),
    .DisplayA(Display_Address), .WriteA(multiplexer_13_out));
  Branch_Unit branch_unit_1 (
    .isBeq(OF_EX_7_q[0]), .isUBranch(OF_EX_7_q[2]), .flags_E(flags_1_flags_e), .isBgt(OF_EX_7_q[1]),
    .flags_GT(flags_1_flags_gt), .isBranchTaken(IsBT));
  Register #(.width(1)) register_5 (.D(control_zero_1_iscall_2), .Q(register_5_q), .clk(Clock));  // open: en, clr
  Register #(.width(1)) register_6 (.D(register_5_q), .Q(register_6_q), .clk(Clock));  // open: en, clr
  Hex_Digit_Display hex_digit_display_4 (.value(register_file_1_displayd[15:12]));  // open: dp
  Hex_Digit_Display hex_digit_display_5 (.value(register_file_1_displayd[19:16]));  // open: dp
  Control_Unit control_unit_1 (
    .isSt(STORE), .isLd(control_unit_1_isld), .isBeq(control_unit_1_isbeq), .isBgt(control_unit_1_isbgt),
    .isRet(RETURN), .I_bit(IF_OF_2_q[26]), .isImmediate(Imme), .opcode(IF_OF_2_q_3),
    .isWb(control_unit_1_iswb), .isUbranch(control_unit_1_isubranch), .isCall(control_unit_1_iscall),
    .ALUsignals(control_unit_1_alusignals));
  // Probe on multiplexer_9_out
  Register #(.width(1)) register_7 (.D(control_zero_1_isret_2), .Q(register_7_q), .clk(Clock));  // open: en, clr
  Register #(.width(13)) OF_EX_6 (.D(control_zero_1_alusignal_2), .Q(OF_EX_6_q), .clk(Clock));  // open: en, clr
  Register #(.width(3)) OF_EX_7 (.D(control_zero_1_isbeq_2), .Q(OF_EX_7_q), .clk(Clock));  // open: en, clr
  Register #(.width(2)) register_8 (
    .D(control_zero_1_isload_2), .Q({St, register_8_q[0]}), .clk(Clock));  // open: en, clr
  Register #(.width(1)) register_9 (.D(register_6_q), .Q(Call), .clk(Clock));  // open: en, clr
  Hex_Digit_Display hex_digit_display_6 (.value(register_file_1_displayd[11:8]));  // open: dp
  Control_Zero control_zero_1 (
    .isUbranch(control_unit_1_isubranch), .isBgt(control_unit_1_isbgt), .isBeq(control_unit_1_isbeq),
    .isCall(control_unit_1_iscall), .isStore(STORE), .isLoad(control_unit_1_isld),
    .ALUsignal(control_unit_1_alusignals), .isImmediate(Imme), .isWb(control_unit_1_iswb), .isRet(RETURN),
    .IsBranchTaken(or_1_out), .isUbranch_2(control_zero_1_isbeq_2[2]), .isBgt_2(control_zero_1_isbeq_2[1]),
    .isBeq_2(control_zero_1_isbeq_2[0]), .isCall_2(control_zero_1_iscall_2),
    .isStore_2(control_zero_1_isload_2[1]), .isLoad_2(control_zero_1_isload_2[0]),
    .ALUsignal_2(control_zero_1_alusignal_2), .isWb_2(control_zero_1_iswb_2), .isRet_2(control_zero_1_isret_2));  // open: isImmediate_2
  Register #(.width(2)) register_10 (.D({St, register_8_q[0]}), .Q(register_10_q), .clk(Clock));  // open: en, clr
  Hex_Digit_Display hex_digit_display_7 (.value(register_file_1_displayd[7:4]));  // open: dp
  Bubble_Adder bubble_adder_1 (
    .Instruction({IF_OF_2_q_3, IF_OF_2_q[26:18], IF_OF_2_q_2, IF_OF_2_q[13:0]}), .isStall(IsStall),
    .Instruction_2(Instruction));
  Multiplexer #(.width(4), .enable("false")) multiplexer_13 (
    .in0(MA_RW_4_q[25:22]), .in1(4'b1111), .out(multiplexer_13_out), .sel(Call));
  Hex_Digit_Display hex_digit_display_8 (.value(register_file_1_displayd[3:0]));  // open: dp
  Register #(.width(32)) OF_EX_8 (.D(Instruction_BL), .Q(Instruction_Post_EX), .clk(Clock));  // open: en, clr
  // Probe on IF_OF_q
  // Probe on Instruction_Post_EX
  // Probe on EX_MA_4_q
  // Probe on MA_RW_4_q
  Register #(.width(32)) EX_MA_4 (.D(Instruction_Post_EX), .Q(EX_MA_4_q), .clk(Clock));  // open: en, clr
  assign M4St = M4 & {2{not_6_out[1]}};  // AND_Gate and_1, 2 bits wide
  Register #(.width(32)) MA_RW_4 (.D(EX_MA_4_q), .Q(MA_RW_4_q), .clk(Clock));  // open: en, clr
  Forwarding_Unit forwarding_unit_1 (
    .IF_OF(IF_OF_q), .OF_EX(Instruction_Post_EX), .EX_MA(EX_MA_4_q), .MA_RW(MA_RW_4_q),
    .RW__OF_2(forwarding_unit_1_rw__of_2), .RW__OF_1(forwarding_unit_1_rw__of_1), .MA__EX_2(M4[1]),
    .MA__EX_1(forwarding_unit_1_rw__ex_1[1]), .RW__EX_2(M4[0]), .RW__EX_1(forwarding_unit_1_rw__ex_1[0]),
    .RW__MA(forwarding_unit_1_rw__ma));
  not not_6 (not_6_out[1], St);

  // Notes on the sheet:
  //   PIPELINED PROCESSOR
  //   isBranchTaken
  //   pc+4
  //   branchTarget
  //   ALUsignals
  //   Branch Lock Unit
  //   B
  //   pc
  //   imm
  //   offset
  //   pc
  //   branchTarget
  //   A
  //   ALU
  //   aluResult
  //   MAR
  //   Memory
  //   Unit
  //   ldResult
  //   Instruction Memory
  //   calc immx
  //   immx
  //   isRet
  //   isBranchTaken
  //   is>
  //   is=
  //   isCmp
  //   M6
  //   MDR
  //   isLd
  //   data
  //   contents of rom_1 (hex, n*v repeats v):
  //   4c000000 4c40000c 7c400000 4c400007 7c400004 4c400004 7c400008 4c40ffef 7c40000c 4c40000f 7c400010
  //   4c40ffdf 7c400014 4c40002d 7c400018 4c800000 4cc00007 9800002f 48008000 74400000 74800004 74c00008
  //   7500000c 75400010 75800014 75c00018 90000000 a0000000 84c0000 15840004 1898000 75180000 75580004
  //   28114000 8800001c c000001 90000001 2c000001 87fffff5 8ffffff5 4800c000 97fffffc 7d180004 7d580000
  //   c000001 2c000001 87fffffa 8800000c 84c0000 15840004 1898000 75180000 75580004 28114000 8ffffff4
  //   c000001 2c000001 88000002 87ffffee 2c000001 87ffffec 8ffffff3 4800c000 97fffffc 97fffffe
  //   M2
  //   Immediate
  //   Flags
  //   isSt
  //   isLd
  //   isCall
  //   M4
  //   M5
  //   rs2
  //   rd
  //   op2
  //   isImmediate
  //   M1
  //   flags(GT)
  //   flags(E)
  //   rs1
  //   isSt
  //   E
  //   Register
  //   A
  //   File
  //   D
  //   op1
  //   Operand 1
  //   M3
  //   Branch
  //   Unit
  //   isRet
  //   isWb
  //   address
  //   data
  //   Display Register
  //   opcode
  //   I bit
  //   isBeq
  //   isBgt
  //   isUBranch
  //   CONTROL
  //   UNIT
  //   instruction
  //   isCall
  //   rd
  //   Forwarding Unit
endmodule

module Control_Unit (
  input  I_bit,
  input  [4:0] opcode,
  output isSt,
  output isLd,
  output isBeq,
  output isBgt,
  output isRet,
  output isImmediate,
  output isWb,
  output isUbranch,
  output isCall,
  output [12:0] ALUsignals
);

  wire and_6_out, and_7_out, and_8_out, and_9_out, and_10_out, and_12_out, and_13_out, nand_1_out;

  nand nand_1 (nand_1_out, opcode[0], opcode[1]);
  and and_1 (isSt, opcode[0], opcode[1], opcode[2], opcode[3], ~opcode[4]);  // AND_Gate
  and and_2 (isLd, ~opcode[0], opcode[1], opcode[2], opcode[3], ~opcode[4]);  // AND_Gate
  and and_3 (isBeq, ~opcode[0], ~opcode[1], ~opcode[2], ~opcode[3], opcode[4]);  // AND_Gate
  and and_4 (isBgt, opcode[0], ~opcode[1], ~opcode[2], ~opcode[3], opcode[4]);  // AND_Gate
  and and_5 (isRet, ~opcode[0], ~opcode[1], opcode[2], ~opcode[3], opcode[4]);  // AND_Gate
  and and_6 (and_6_out, opcode[0], ~opcode[1], opcode[2], ~opcode[4]);  // AND_Gate
  and and_7 (and_7_out, opcode[0], opcode[2], opcode[3], ~opcode[4]);  // AND_Gate
  and and_8 (and_8_out, opcode[4], nand_1_out);
  and and_9 (and_9_out, opcode[1], ~opcode[2], ~opcode[3], opcode[4]);  // AND_Gate
  and and_10 (and_10_out, ~opcode[0], ~opcode[1], opcode[2], ~opcode[3], opcode[4]);  // AND_Gate
  and and_11 (isCall, opcode[0], opcode[1], ~opcode[2], ~opcode[3], opcode[4]);  // AND_Gate
  and and_12 (and_12_out, ~opcode[0], ~opcode[1], ~opcode[2], ~opcode[3], ~opcode[4]);  // AND_Gate
  and and_13 (and_13_out, opcode[1], opcode[2], opcode[3], ~opcode[4]);  // AND_Gate
  and isSub (ALUsignals[2], opcode[0], ~opcode[1], ~opcode[2], ~opcode[3], ~opcode[4]);  // AND_Gate
  and isCmp (ALUsignals[0], opcode[0], ~opcode[1], opcode[2], ~opcode[3], ~opcode[4]);  // AND_Gate
  and isMul (ALUsignals[3], ~opcode[0], opcode[1], ~opcode[2], ~opcode[3], ~opcode[4]);  // AND_Gate
  and isDiv (ALUsignals[4], opcode[0], opcode[1], ~opcode[2], ~opcode[3], ~opcode[4]);  // AND_Gate
  and isMod (ALUsignals[5], ~opcode[0], ~opcode[1], opcode[2], ~opcode[3], ~opcode[4]);  // AND_Gate
  and isLsl (ALUsignals[7], ~opcode[0], opcode[1], ~opcode[2], opcode[3], ~opcode[4]);  // AND_Gate
  and isLsr (ALUsignals[8], opcode[0], opcode[1], ~opcode[2], opcode[3], ~opcode[4]);  // AND_Gate
  and isAsr (ALUsignals[9], ~opcode[0], ~opcode[1], opcode[2], opcode[3], ~opcode[4]);  // AND_Gate
  and isOr (ALUsignals[12], opcode[0], opcode[1], opcode[2], ~opcode[3], ~opcode[4]);  // AND_Gate
  and isAnd (ALUsignals[11], ~opcode[0], opcode[1], opcode[2], ~opcode[3], ~opcode[4]);  // AND_Gate
  and isNot (ALUsignals[10], ~opcode[0], ~opcode[1], ~opcode[2], opcode[3], ~opcode[4]);  // AND_Gate
  and isMov (ALUsignals[6], opcode[0], ~opcode[1], ~opcode[2], opcode[3], ~opcode[4]);  // AND_Gate
  or or_1 (isUbranch, and_9_out, and_10_out);
  or isAdd (ALUsignals[1], and_12_out, and_13_out);
  nor nor_1 (isWb, and_6_out, and_7_out, and_8_out);

  assign isImmediate = I_bit;

  // Notes on the sheet:
  //   op1
  //   op2
  //   op3
  //   op4
  //   op5
endmodule

module Register_File (
  input  Clock,
  input  Reset,
  input  [31:0] WriteD,
  input  [3:0] ReadA1,
  input  WriteE,
  input  [3:0] WriteA,
  input  [3:0] ReadA2,
  input  [3:0] DisplayA,
  output [31:0] ReadD1,
  output [31:0] ReadD2,
  output [31:0] DisplayD
);

  wire demultiplexer_1_out0, demultiplexer_1_out1, demultiplexer_1_out2, demultiplexer_1_out3,
       demultiplexer_1_out4, demultiplexer_1_out5, demultiplexer_1_out6, demultiplexer_1_out7,
       demultiplexer_1_out8, demultiplexer_1_out9, demultiplexer_1_out10, demultiplexer_1_out11,
       demultiplexer_1_out12, demultiplexer_1_out13, demultiplexer_1_out14, demultiplexer_1_out15,
       multiplexer_2_out, or_1_out, or_2_out;
  wire [31:0] multiplexer_1_out, r0_q, r1_q, r2_q, r3_q, r4_q, r5_q, r6_q, r7_q, r8_q, r9_q, r10_q, r11_q,
       r12_q, r13_q, r14_q, r15_q;

  Demultiplexer #(.select(4), .disabled(0), .enable("false")) demultiplexer_1 (
    .out0(demultiplexer_1_out0), .out1(demultiplexer_1_out1), .out2(demultiplexer_1_out2),
    .out3(demultiplexer_1_out3), .out4(demultiplexer_1_out4), .out5(demultiplexer_1_out5),
    .out6(demultiplexer_1_out6), .out7(demultiplexer_1_out7), .out8(demultiplexer_1_out8),
    .out9(demultiplexer_1_out9), .out10(demultiplexer_1_out10), .out11(demultiplexer_1_out11),
    .out12(demultiplexer_1_out12), .out13(demultiplexer_1_out13), .out14(demultiplexer_1_out14),
    .out15(demultiplexer_1_out15), .in(WriteE), .sel(WriteA));
  Multiplexer #(.width(32), .enable("false")) multiplexer_1 (
    .in0(WriteD), .in1(32'h3fffffc), .out(multiplexer_1_out), .sel(Reset));
  or or_1 (or_1_out, demultiplexer_1_out14, Reset);
  Multiplexer #(.enable("false")) multiplexer_2 (.in0(or_2_out), .out(multiplexer_2_out), .sel(1'b0));  // open: in1
  or or_2 (or_2_out, Clock, Reset);
  Register #(.width(32)) r0 (.D(WriteD), .en(demultiplexer_1_out0), .Q(r0_q), .clk(Clock), .clr(Reset));
  Register #(.width(32)) r1 (.D(WriteD), .en(demultiplexer_1_out1), .Q(r1_q), .clk(Clock), .clr(Reset));
  Register #(.width(32)) r2 (.D(WriteD), .en(demultiplexer_1_out2), .Q(r2_q), .clk(Clock), .clr(Reset));
  Register #(.width(32)) r3 (.D(WriteD), .en(demultiplexer_1_out3), .Q(r3_q), .clk(Clock), .clr(Reset));
  Register #(.width(32)) r4 (.D(WriteD), .en(demultiplexer_1_out4), .Q(r4_q), .clk(Clock), .clr(Reset));
  Register #(.width(32)) r5 (.D(WriteD), .en(demultiplexer_1_out5), .Q(r5_q), .clk(Clock), .clr(Reset));
  Register #(.width(32)) r6 (.D(WriteD), .en(demultiplexer_1_out6), .Q(r6_q), .clk(Clock), .clr(Reset));
  Register #(.width(32)) r7 (.D(WriteD), .en(demultiplexer_1_out7), .Q(r7_q), .clk(Clock), .clr(Reset));
  Register #(.width(32)) r8 (.D(WriteD), .en(demultiplexer_1_out8), .Q(r8_q), .clk(Clock), .clr(Reset));
  Register #(.width(32)) r9 (.D(WriteD), .en(demultiplexer_1_out9), .Q(r9_q), .clk(Clock), .clr(Reset));
  Register #(.width(32)) r10 (.D(WriteD), .en(demultiplexer_1_out10), .Q(r10_q), .clk(Clock), .clr(Reset));
  Register #(.width(32)) r11 (.D(WriteD), .en(demultiplexer_1_out11), .Q(r11_q), .clk(Clock), .clr(Reset));
  Register #(.width(32)) r12 (.D(WriteD), .en(demultiplexer_1_out12), .Q(r12_q), .clk(Clock), .clr(Reset));
  Register #(.width(32)) r13 (.D(WriteD), .en(demultiplexer_1_out13), .Q(r13_q), .clk(Clock), .clr(Reset));
  Register #(.width(32)) r14 (.D(multiplexer_1_out), .en(or_1_out), .Q(r14_q), .clk(multiplexer_2_out));  // open: clr
  Register #(.width(32)) r15 (.D(WriteD), .en(demultiplexer_1_out15), .Q(r15_q), .clk(Clock), .clr(Reset));
  Multiplexer #(.select(4), .width(32), .disabled(0), .enable("false")) multiplexer_3 (
    .in0(r0_q), .in1(r1_q), .in2(r2_q), .in3(r3_q), .in4(r4_q), .in5(r5_q), .in6(r6_q), .in7(r7_q),
    .in8(r8_q), .in9(r9_q), .in10(r10_q), .in11(r11_q), .in12(r12_q), .in13(r13_q), .in14(r14_q),
    .in15(r15_q), .out(ReadD1), .sel(ReadA1));
  Multiplexer #(.select(4), .width(32), .disabled(0), .enable("false")) multiplexer_4 (
    .in0(r0_q), .in1(r1_q), .in2(r2_q), .in3(r3_q), .in4(r4_q), .in5(r5_q), .in6(r6_q), .in7(r7_q),
    .in8(r8_q), .in9(r9_q), .in10(r10_q), .in11(r11_q), .in12(r12_q), .in13(r13_q), .in14(r14_q),
    .in15(r15_q), .out(ReadD2), .sel(ReadA2));
  Multiplexer #(.select(4), .width(32), .disabled(0), .enable("false")) multiplexer_5 (
    .in0(r0_q), .in1(r1_q), .in2(r2_q), .in3(r3_q), .in4(r4_q), .in5(r5_q), .in6(r6_q), .in7(r7_q),
    .in8(r8_q), .in9(r9_q), .in10(r10_q), .in11(r11_q), .in12(r12_q), .in13(r13_q), .in14(r14_q),
    .in15(r15_q), .out(DisplayD), .sel(DisplayA));
endmodule

module ALU (
  input  [31:0] A,
  input  [31:0] B,
  input  [12:0] ALUsignals,
  output [31:0] aluResult,
  output is,
  output is_2
);

  wire [31:0] adder_1_out, and_1_out, divider_1_out, divider_1_rem, multiplier_1_out, not_1_out, or_1_out,
       shifter_1_out, shifter_2_out, shifter_3_out, subtractor_1_out;

  Adder #(.width(32)) adder_1 (.a(A), .b(B), .out(adder_1_out));  // open: cin, cout
  Subtractor #(.width(32)) subtractor_1 (.a(A), .b(B), .out(subtractor_1_out));  // open: bin, bout
  Multiplier #(.width(32)) multiplier_1 (.a(A), .b(B), .out(multiplier_1_out));  // open: cin, cout
  Divider #(.width(32)) divider_1 (.a(A), .b(B), .out(divider_1_out), .rem(divider_1_rem));  // open: upper
  Comparator #(.width(32)) comparator_1 (.a(A), .b(B), .gt(is), .eq(is_2));  // open: lt
  Shifter #(.width(32)) shifter_1 (.in(A), .\dist (B[4:0]), .out(shifter_1_out));
  Shifter #(.width(32), .shift("lr")) shifter_2 (.in(A), .\dist (B[4:0]), .out(shifter_2_out));
  Shifter #(.width(32), .shift("ar")) shifter_3 (.in(A), .\dist (B[4:0]), .out(shifter_3_out));
  assign not_1_out = ~B;  // NOT_Gate not_1, 32 bits wide
  assign and_1_out = A & B;  // AND_Gate and_1, 32 bits wide
  assign or_1_out = A | B;  // OR_Gate or_1, 32 bits wide
  assign aluResult = ALUsignals[1] ? adder_1_out : 32'bz;  // Controlled_Buffer controlled_buffer_1
  assign aluResult = ALUsignals[2] ? subtractor_1_out : 32'bz;  // Controlled_Buffer controlled_buffer_2
  assign aluResult = ALUsignals[3] ? multiplier_1_out : 32'bz;  // Controlled_Buffer controlled_buffer_3
  assign aluResult = ALUsignals[4] ? divider_1_out : 32'bz;  // Controlled_Buffer controlled_buffer_4
  assign aluResult = ALUsignals[5] ? divider_1_rem : 32'bz;  // Controlled_Buffer controlled_buffer_5
  assign aluResult = ALUsignals[6] ? B : 32'bz;  // Controlled_Buffer controlled_buffer_6
  assign aluResult = ALUsignals[7] ? shifter_1_out : 32'bz;  // Controlled_Buffer controlled_buffer_7
  assign aluResult = ALUsignals[8] ? shifter_2_out : 32'bz;  // Controlled_Buffer controlled_buffer_8
  assign aluResult = ALUsignals[9] ? shifter_3_out : 32'bz;  // Controlled_Buffer controlled_buffer_9
  assign aluResult = ALUsignals[10] ? not_1_out : 32'bz;  // Controlled_Buffer controlled_buffer_10
  assign aluResult = ALUsignals[11] ? and_1_out : 32'bz;  // Controlled_Buffer controlled_buffer_11
  assign aluResult = ALUsignals[12] ? or_1_out : 32'bz;  // Controlled_Buffer controlled_buffer_12

  // Notes on the sheet:
  //   add
  //   sub
  //   mul
  //   div
  //   cmp
  //   lsr
  //   mod
  //   lsl
  //   asr
endmodule

module Flags (
  input  isCmp,
  input  is,
  input  is_2,
  output flags_GT,
  output flags_E
);

  D_Flip_Flop #(.trigger("high")) d_ff_1 (.clk(isCmp), .D(is), .Q(flags_GT));  // open: Qn, preset, en, reset
  D_Flip_Flop #(.trigger("high")) d_ff_2 (.clk(isCmp), .D(is_2), .Q(flags_E));  // open: Qn, preset, en, reset
endmodule

module Branch_Unit (
  input  isUBranch,
  input  isBeq,
  input  flags_E,
  input  isBgt,
  input  flags_GT,
  output isBranchTaken
);

  wire and_1_out, and_2_out;

  and and_1 (and_1_out, isBeq, flags_E);
  and and_2 (and_2_out, isBgt, flags_GT);
  or or_1 (isBranchTaken, isUBranch, and_1_out, and_2_out);
endmodule

module Memory_Unit (
  input  [31:0] MAR,
  input  isLd,
  input  [31:0] MDR,
  input  isSt,
  input  Clock,
  input  Reset,
  output [31:0] ldResult
);

  RAM #(.addrWidth(24), .dataWidth(32), .bus("separate")) ram_1 (
    .addr(MAR[25:2]), .din(MDR), .data(ldResult), .str(isSt), .clk(Clock), .ld(isLd), .clr(Reset));  // open: sel
endmodule

module Calculate_Immediate (
  input  [17:0] imm,
  output [31:0] immx
);

  wire [31:0] bit_extender_1_out, bit_extender_2_out, shifter_1_out;

  assign bit_extender_1_out = {{16{1'b0}}, imm[15:0]};  // Bit_Extender bit_extender_1
  assign bit_extender_2_out = {{16{imm[15]}}, imm[15:0]};  // Bit_Extender bit_extender_2
  Shifter #(.width(32)) shifter_1 (.in(bit_extender_1_out), .\dist (5'b10000), .out(shifter_1_out));
  Multiplexer #(.select(2), .width(32), .enable("false")) multiplexer_1 (
    .in0(bit_extender_2_out), .in1(bit_extender_1_out), .in2(shifter_1_out), .out(immx), .sel(imm[17:16]));  // open: in3

  // Notes on the sheet:
  //   modifier bits
  //   high
  //   default
  //   unsigned
endmodule

module FW1 (
  input  [31:0] A,
  input  [31:0] B,
  output isConflict
);

  wire and_1_out, and_2_out, and_4_out, and_5_out, and_6_out, and_7_out, and_8_out, and_9_out, and_10_out,
       and_11_out, and_12_out, not_1_out, not_2_out, not_3_out, not_4_out, not_5_out, not_6_out, not_7_out,
       not_8_out, not_9_out, not_10_out, not_11_out, not_12_out, not_13_out, not_14_out, or_1_out, or_2_out,
       xor_1_out, xor_2_out, xor_3_out, xor_4_out;
  wire [3:0] multiplexer_1_out, multiplexer_2_out;
  wire [31:0] xnor_1_out, xnor_2_out;

  not not_1 (not_1_out, A[29]);
  not not_2 (not_2_out, A[28]);
  assign xnor_1_out = ~(A ^ {32{1'b0}});  // XNOR_Gate xnor_1, 32 bits wide
  assign xnor_2_out = ~(B ^ {32{1'b0}});  // XNOR_Gate xnor_2, 32 bits wide
  not not_3 (not_3_out, A[31]);
  not not_4 (not_4_out, B[28]);
  not not_5 (not_5_out, and_1_out);
  and and_1 (and_1_out, B[28], B[27]);
  not not_6 (not_6_out, A[27]);
  and and_2 (and_2_out, A[31], not_1_out);
  // AND_Gate and_3 has open pins: in0=not_3_out, in1=A[30], in2=not_1_out, in3=not_2_out, out=open
  and and_4 (and_4_out, A[30], A[29], not_2_out, A[27]);
  and and_5 (and_5_out, B[30], B[29], B[28], B[27]);
  and and_6 (and_6_out, B[29], not_4_out, B[27]);
  and and_7 (and_7_out, B[31], not_5_out);
  and and_8 (and_8_out, A[31], not_3_out, A[29], not_2_out, not_6_out);
  or or_1 (or_1_out, and_2_out, 1'b0, and_4_out);
  and and_9 (and_9_out, B[31], B[28], B[27]);
  or or_2 (or_2_out, and_5_out, and_6_out, and_7_out);
  not not_7 (not_7_out, or_1_out);
  not not_8 (not_8_out, or_2_out);
  Multiplexer #(.width(4), .enable("false")) multiplexer_1 (
    .in0({A[18], A[19], A[20], A[21]}), .in1(4'b1111), .out(multiplexer_1_out), .sel(and_8_out));
  Multiplexer #(.width(4), .enable("false")) multiplexer_2 (
    .in0({B[22], B[23], B[24], B[25]}), .in1(4'b1111), .out(multiplexer_2_out), .sel(and_9_out));
  not not_9 (not_9_out, xor_1_out);
  xor xor_1 (xor_1_out, multiplexer_1_out[2], multiplexer_2_out[2]);
  xor xor_2 (xor_2_out, multiplexer_1_out[0], multiplexer_2_out[0]);
  not not_10 (not_10_out, xor_2_out);
  xor xor_3 (xor_3_out, multiplexer_1_out[1], multiplexer_2_out[1]);
  not not_11 (not_11_out, xor_3_out);
  not not_12 (not_12_out, xor_4_out);
  xor xor_4 (xor_4_out, multiplexer_1_out[3], multiplexer_2_out[3]);
  and and_10 (and_10_out, not_9_out, not_10_out, not_11_out, not_12_out);
  and and_11 (and_11_out, xnor_1_out[31], xnor_1_out[30], xnor_1_out[29], xnor_1_out[28], xnor_1_out[27], xnor_1_out[26], xnor_1_out[25], xnor_1_out[24], xnor_1_out[23], xnor_1_out[22], xnor_1_out[21], xnor_1_out[20], xnor_1_out[19], xnor_1_out[18], xnor_1_out[17], xnor_1_out[16], xnor_1_out[14], xnor_1_out[13], xnor_1_out[12], xnor_1_out[11], xnor_1_out[10], xnor_1_out[9], xnor_1_out[8], xnor_1_out[7], xnor_1_out[6], xnor_1_out[5], xnor_1_out[4], xnor_1_out[3], xnor_1_out[2], xnor_1_out[1], xnor_1_out[0], xnor_1_out[15]);
  and and_12 (and_12_out, xnor_2_out[31], xnor_2_out[30], xnor_2_out[29], xnor_2_out[28], xnor_2_out[27], xnor_2_out[26], xnor_2_out[25], xnor_2_out[24], xnor_2_out[23], xnor_2_out[22], xnor_2_out[21], xnor_2_out[20], xnor_2_out[19], xnor_2_out[18], xnor_2_out[17], xnor_2_out[16], xnor_2_out[14], xnor_2_out[13], xnor_2_out[12], xnor_2_out[11], xnor_2_out[10], xnor_2_out[9], xnor_2_out[8], xnor_2_out[7], xnor_2_out[6], xnor_2_out[5], xnor_2_out[4], xnor_2_out[3], xnor_2_out[2], xnor_2_out[1], xnor_2_out[0], xnor_2_out[15]);
  not not_13 (not_13_out, and_11_out);
  and and_13 (isConflict, not_13_out, not_7_out, and_10_out, not_8_out, not_14_out);
  not not_14 (not_14_out, and_12_out);

  // Notes on the sheet:
  //   b..
  //   not-mov
  //   nop
  //   st
  //   cmp-nop
  //   b..
  //   ret
  //   call
  //   src 1
  //   dest
  //   src1==dest
endmodule

module FW2 (
  input  [31:0] in_1,
  input  [31:0] in_2,
  output isConflict
);

  wire and_1_out, and_2_out, and_3_out, and_4_out, and_5_out, and_6_out, and_7_out, and_8_out, and_9_out,
       and_10_out, and_11_out, and_12_out, not_1_out, not_2_out, not_3_out, not_4_out, not_5_out, not_6_out,
       not_7_out, not_8_out, not_9_out, not_10_out, or_1_out, or_2_out, xnor_3_out, xnor_4_out, xnor_5_out,
       xnor_6_out;
  wire [3:0] multiplexer_1_out, multiplexer_2_out;
  wire [31:0] xnor_1_out, xnor_2_out;

  assign xnor_1_out = ~(in_1 ^ {32{1'b0}});  // XNOR_Gate xnor_1, 32 bits wide
  assign xnor_2_out = ~(in_2 ^ {32{1'b0}});  // XNOR_Gate xnor_2, 32 bits wide
  not not_1 (not_1_out, in_1[29]);
  not not_2 (not_2_out, in_1[28]);
  not not_3 (not_3_out, in_2[28]);
  and and_1 (and_1_out, in_2[28], in_2[27]);
  not not_4 (not_4_out, in_2[30]);
  not not_5 (not_5_out, in_1[30]);
  and and_2 (and_2_out, in_1[31], not_5_out, not_1_out);
  and and_3 (and_3_out, in_1[30], in_1[29], not_2_out, in_1[27]);
  and and_4 (and_4_out, in_2[30], in_2[29], not_3_out, in_2[27]);
  and and_5 (and_5_out, in_2[31], and_1_out);
  and and_6 (and_6_out, in_2[31], not_4_out, in_2[29]);
  and and_7 (and_7_out, in_2[30], in_2[29], in_2[28], in_2[27]);
  and and_8 (and_8_out, in_1[30], in_1[29], in_1[28], in_1[27]);
  Multiplexer #(.width(4), .enable("false")) multiplexer_1 (
    .in0(in_2[25:22]), .in1(4'b1111), .out(multiplexer_1_out), .sel(and_5_out));
  not not_6 (not_6_out, and_8_out);
  and and_9 (and_9_out, not_6_out, in_1[26]);
  or or_1 (or_1_out, and_4_out, and_5_out, and_6_out, and_7_out);
  or or_2 (or_2_out, and_2_out, and_3_out, and_9_out);
  Multiplexer #(.width(4), .enable("false")) multiplexer_2 (
    .in0(in_1[17:14]), .in1(in_1[25:22]), .out(multiplexer_2_out), .sel(and_8_out));
  not not_7 (not_7_out, or_1_out);
  not not_8 (not_8_out, or_2_out);
  xnor xnor_3 (xnor_3_out, multiplexer_2_out[3], multiplexer_1_out[3]);
  xnor xnor_4 (xnor_4_out, multiplexer_2_out[2], multiplexer_1_out[2]);
  xnor xnor_5 (xnor_5_out, multiplexer_2_out[1], multiplexer_1_out[1]);
  xnor xnor_6 (xnor_6_out, multiplexer_2_out[0], multiplexer_1_out[0]);
  and and_10 (and_10_out, xnor_3_out, xnor_4_out, xnor_5_out, xnor_6_out);
  and and_11 (and_11_out, xnor_1_out[31], xnor_1_out[30], xnor_1_out[29], xnor_1_out[28], xnor_1_out[27], xnor_1_out[26], xnor_1_out[25], xnor_1_out[24], xnor_1_out[23], xnor_1_out[22], xnor_1_out[21], xnor_1_out[20], xnor_1_out[19], xnor_1_out[18], xnor_1_out[17], xnor_1_out[16], xnor_1_out[14], xnor_1_out[13], xnor_1_out[12], xnor_1_out[11], xnor_1_out[10], xnor_1_out[9], xnor_1_out[8], xnor_1_out[7], xnor_1_out[6], xnor_1_out[5], xnor_1_out[4], xnor_1_out[3], xnor_1_out[2], xnor_1_out[1], xnor_1_out[0], xnor_1_out[15]);
  and and_12 (and_12_out, xnor_2_out[31], xnor_2_out[30], xnor_2_out[29], xnor_2_out[28], xnor_2_out[27], xnor_2_out[26], xnor_2_out[25], xnor_2_out[24], xnor_2_out[23], xnor_2_out[22], xnor_2_out[21], xnor_2_out[20], xnor_2_out[19], xnor_2_out[18], xnor_2_out[17], xnor_2_out[16], xnor_2_out[14], xnor_2_out[13], xnor_2_out[12], xnor_2_out[11], xnor_2_out[10], xnor_2_out[9], xnor_2_out[8], xnor_2_out[7], xnor_2_out[6], xnor_2_out[5], xnor_2_out[4], xnor_2_out[3], xnor_2_out[2], xnor_2_out[1], xnor_2_out[0], xnor_2_out[15]);
  not not_9 (not_9_out, and_11_out);
  and and_13 (isConflict, not_9_out, not_8_out, not_7_out, and_10_out, not_10_out);
  not not_10 (not_10_out, and_12_out);

  // Notes on the sheet:
  //   A
  //   B
  //   b..
  //   nop
  //   st
  //   nop
  //   call
  //   b..
  //   st
  //   rd
  //   rs2
  //   rd
  //   ra
  //   dest
  //   src2
  //   src2==dest
endmodule

module Forwarding_Unit (
  input  [31:0] IF_OF,
  input  [31:0] OF_EX,
  input  [31:0] EX_MA,
  input  [31:0] MA_RW,
  output RW__OF_2,
  output RW__OF_1,
  output MA__EX_2,
  output MA__EX_1,
  output RW__EX_2,
  output RW__EX_1,
  output RW__MA
);

  FW2 FW2 (.in_1(IF_OF), .in_2(MA_RW), .isConflict(RW__OF_2));
  FW1 FW1 (.A(IF_OF), .B(MA_RW), .isConflict(RW__OF_1));
  FW2 FW2_2 (.in_1(OF_EX), .in_2(MA_RW), .isConflict(RW__EX_2));
  FW1 FW1_2 (.A(OF_EX), .B(MA_RW), .isConflict(RW__EX_1));
  FW2 FW2_3 (.in_1(EX_MA), .in_2(MA_RW), .isConflict(RW__MA));
  FW2 FW2_4 (.in_1(OF_EX), .in_2(EX_MA), .isConflict(MA__EX_2));
  FW1 FW1_3 (.A(OF_EX), .B(EX_MA), .isConflict(MA__EX_1));
endmodule

module Branch_Lock (
  input  [31:0] Instruction,
  input  [31:0] Branch_Target,
  input  [31:0] Immediate,
  input  [31:0] Operand,
  input  is_branch_taken,
  output [31:0] Instruction_2,
  output [31:0] Branch_Target_2,
  output [31:0] Immediate_2,
  output [31:0] Operand_2
);

  Multiplexer #(.width(32), .enable("false")) multiplexer_1 (
    .in0(Instruction), .in1(32'h68000000), .out(Instruction_2), .sel(is_branch_taken));
  Multiplexer #(.width(32), .enable("false")) multiplexer_2 (
    .in0(Branch_Target), .in1({32{1'b0}}), .out(Branch_Target_2), .sel(is_branch_taken));
  Multiplexer #(.width(32), .enable("false")) multiplexer_3 (
    .in0(Immediate), .in1({32{1'b0}}), .out(Immediate_2), .sel(is_branch_taken));
  Multiplexer #(.width(32), .enable("false")) multiplexer_4 (
    .in0(Operand), .in1({32{1'b0}}), .out(Operand_2), .sel(is_branch_taken));
endmodule

module Control_Zero (
  input  isUbranch,
  input  isBgt,
  input  isBeq,
  input  isCall,
  input  isStore,
  input  isLoad,
  input  [12:0] ALUsignal,
  input  isImmediate,
  input  isWb,
  input  isRet,
  input  IsBranchTaken,
  output isUbranch_2,
  output isBgt_2,
  output isBeq_2,
  output isCall_2,
  output isStore_2,
  output isLoad_2,
  output [12:0] ALUsignal_2,
  output isImmediate_2,
  output isWb_2,
  output isRet_2
);

  Multiplexer #(.enable("false")) multiplexer_1 (.in0(isRet), .in1(1'b0), .out(isRet_2), .sel(IsBranchTaken));
  Multiplexer #(.enable("false")) multiplexer_2 (.in0(isWb), .in1(1'b0), .out(isWb_2), .sel(IsBranchTaken));
  Multiplexer #(.enable("false")) multiplexer_3 (
    .in0(isImmediate), .in1(1'b0), .out(isImmediate_2), .sel(IsBranchTaken));
  Multiplexer #(.width(13), .enable("false")) multiplexer_4 (
    .in0(ALUsignal), .in1({13{1'b0}}), .out(ALUsignal_2), .sel(IsBranchTaken));
  Multiplexer #(.enable("false")) multiplexer_5 (.in0(isLoad), .in1(1'b0), .out(isLoad_2), .sel(IsBranchTaken));
  Multiplexer #(.enable("false")) multiplexer_6 (.in0(isStore), .in1(1'b0), .out(isStore_2), .sel(IsBranchTaken));
  Multiplexer #(.enable("false")) multiplexer_7 (.in0(isCall), .in1(1'b0), .out(isCall_2), .sel(IsBranchTaken));
  Multiplexer #(.enable("false")) multiplexer_8 (.in0(isBeq), .in1(1'b0), .out(isBeq_2), .sel(IsBranchTaken));
  Multiplexer #(.enable("false")) multiplexer_9 (.in0(isBgt), .in1(1'b0), .out(isBgt_2), .sel(IsBranchTaken));
  Multiplexer #(.enable("false")) multiplexer_10 (.in0(isUbranch), .in1(1'b0), .out(isUbranch_2), .sel(IsBranchTaken));
endmodule

module Bubble_Adder (
  input  [31:0] Instruction,
  input  isStall,
  output [31:0] Instruction_2
);

  Multiplexer #(.width(32), .enable("false")) multiplexer_1 (
    .in0(Instruction), .in1(32'h68000000), .out(Instruction_2), .sel(isStall));
endmodule

module Load_Use (
  input  [31:0] A,
  input  [31:0] B,
  output is_Stall
);

  wire and_1_out, and_2_out, and_3_out, and_4_out, and_5_out, and_6_out, and_7_out, and_8_out, and_9_out,
       and_10_out, and_11_out, and_12_out, Ld_out, not_1_out, not_2_out, not_3_out, not_4_out, not_5_out,
       not_6_out, not_7_out, not_8_out, not_9_out, not_10_out, not_11_out, not_12_out, not_13_out,
       not_14_out, not_15_out, or_1_out, xnor_2_out, xnor_3_out, xnor_4_out, xnor_5_out, xnor_6_out,
       xnor_7_out, xnor_8_out, xnor_9_out;
  wire [3:0] multiplexer_1_out, multiplexer_2_out;
  wire [31:0] xnor_1_out;

  not not_1 (not_1_out, A[30]);
  and and_1 (and_1_out, A[31], not_1_out, A[29], not_2_out, not_3_out);
  not not_2 (not_2_out, A[28]);
  not not_3 (not_3_out, A[27]);
  not not_4 (not_4_out, B[27]);
  not not_5 (not_5_out, A[31]);
  and and_2 (and_2_out, not_5_out, A[30], not_6_out, not_7_out);
  not not_6 (not_6_out, A[29]);
  not not_7 (not_7_out, A[28]);
  assign xnor_1_out = ~(A ^ {32{1'b0}});  // XNOR_Gate xnor_1, 32 bits wide
  and Ld (Ld_out, B[30], B[29], B[28], not_4_out);
  not not_8 (not_8_out, and_2_out);
  not not_9 (not_9_out, A[29]);
  not not_10 (not_10_out, A[28]);
  and and_3 (and_3_out, A[31], not_11_out, not_9_out);
  not not_11 (not_11_out, A[30]);
  and and_4 (and_4_out, A[30], A[29], not_10_out, A[27]);
  and and_5 (and_5_out, A[30], A[29], A[28], A[27]);
  Multiplexer #(.width(4), .enable("false")) multiplexer_1 (
    .in0(A[21:18]), .in1(4'b1111), .out(multiplexer_1_out), .sel(and_1_out));
  not not_12 (not_12_out, and_5_out);
  not not_13 (not_13_out, A[26]);
  and and_6 (and_6_out, and_3_out, and_4_out);
  and and_7 (and_7_out, not_12_out, not_13_out);
  Multiplexer #(.width(4), .enable("false")) multiplexer_2 (
    .in0(A[17:14]), .in1(A[25:22]), .out(multiplexer_2_out), .sel(and_5_out));
  not not_14 (not_14_out, and_6_out);
  xnor xnor_2 (xnor_2_out, multiplexer_2_out[3], B[25]);
  xnor xnor_3 (xnor_3_out, multiplexer_2_out[2], B[24]);
  xnor xnor_4 (xnor_4_out, multiplexer_2_out[1], B[23]);
  xnor xnor_5 (xnor_5_out, multiplexer_2_out[0], B[22]);
  xnor xnor_6 (xnor_6_out, multiplexer_1_out[3], B[25]);
  xnor xnor_7 (xnor_7_out, multiplexer_1_out[2], B[24]);
  xnor xnor_8 (xnor_8_out, multiplexer_1_out[1], B[23]);
  xnor xnor_9 (xnor_9_out, multiplexer_1_out[0], B[22]);
  and and_8 (and_8_out, xnor_2_out, xnor_3_out, xnor_4_out, xnor_5_out);
  and and_9 (and_9_out, xnor_6_out, xnor_7_out, xnor_8_out, xnor_9_out);
  and and_10 (and_10_out, and_7_out, and_8_out);
  and and_11 (and_11_out, not_8_out, and_9_out);
  and and_12 (and_12_out, xnor_1_out[31], xnor_1_out[30], xnor_1_out[29], xnor_1_out[28], xnor_1_out[27], xnor_1_out[26], xnor_1_out[25], xnor_1_out[24], xnor_1_out[23], xnor_1_out[22], xnor_1_out[21], xnor_1_out[20], xnor_1_out[19], xnor_1_out[18], xnor_1_out[17], xnor_1_out[16], xnor_1_out[14], xnor_1_out[13], xnor_1_out[12], xnor_1_out[11], xnor_1_out[10], xnor_1_out[9], xnor_1_out[8], xnor_1_out[7], xnor_1_out[6], xnor_1_out[5], xnor_1_out[4], xnor_1_out[3], xnor_1_out[2], xnor_1_out[1], xnor_1_out[0], xnor_1_out[15]);
  or or_1 (or_1_out, and_10_out, and_11_out);
  not not_15 (not_15_out, and_12_out);
  and and_13 (is_Stall, not_14_out, Ld_out, not_15_out, or_1_out);

  // Notes on the sheet:
  //   A
  //   B
  //   ret
  //   not-mov
  //   rs1
  //   dest
  //   has src1
  //   b..
  //   nop
  //   st
  //   src1
  //   rd
  //   rs2
  //   src2
  //   has src2
  //   src1==dest
  //   src2==dest
endmodule
